# Fritzing sketch controller circuit (saved by Fritzing 1.0.3b)
breadboards: 1

parts:
  U1 = ESP8266 WiFi Module [part_number=ESP8266]
  U2 = V_REG_LD1117VXX [package=78xxl]
  LED_array_-_Bright_temp = LEDs [package=led10mm]
  LED_array_-_warm_temp = LEDs [package=led10mm]
  Q1 = NPN-Transistor [package="TO92 [THT]"]
  Q2 = NPN-Transistor [package="TO92 [THT]"]
  R1 = Resistor [tolerance=±5% power=0.25W resistance=1000 package=THT]
  R2 = Resistor [tolerance=±5% power=0.25W resistance=1000 package=THT]

nets:
  N1: U1.VCC, U1.CH_PD, U2.OUT
  GND: U1.GND, U1.GPIO_15, U2.GND, Q1.E, Q2.E
  N2: U1.GPIO_4, R1.Pin_0
  N3: U1.GPIO_5, R2.Pin_0
  N4: U2.IN, LED_array_-_Bright_temp.A, LED_array_-_warm_temp.A
  N5: LED_array_-_Bright_temp.C, Q2.C
  N6: LED_array_-_warm_temp.C, Q1.C
  N7: Q1.B, R2.Pin_1
  N8: Q2.B, R1.Pin_1
